# Fritzing sketch digital-light-pulse-sensor (saved by Fritzing 0.9.3b)
breadboards: 1

parts:
  Part1 = Adafruit T-Cobbler Plus [part_number="Adafruit #1989 and #2028"]
  R4 = Resistor [tolerance=±5% resistance=1k package=THT]
  R3 = Resistor [tolerance=±5% resistance=10k package=THT]
  Q1 = NPN-Transistor [part_number=BC547B package="TO92 [THT]"]
  R5 = Resistor [tolerance=±5% resistance=100 package=THT]
  R6 = Photocell (LDR) [package=THT]

nets:
  N1: Part1.GND, Q1.E, R5.Pin_1
  N2: Part1.+3.3V_2, R3.Pin_1, R6.pin_0
  N3: Part1.GPIO23, R4.Pin_0
  N4: R4.Pin_1, R3.Pin_0, Q1.C
  N5: Q1.B, R5.Pin_0, R6.pin_1

custom parts:
  Adafruit T-Cobbler Plus: The Raspberry Pi has landed on the Maker World like a 40-GPIO pinned, quad-USB ported, credit card sized bomb of DIY joy. And while you can use most of our great Model B accessories by hooking up our downgrade cable, its probably a good time to upgrade your set up and accessorize using all of the 40 pins. That's why we now carry the Assembled Adafruit Pi T-Cobbler Plus - Breakout + Cable for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
